# Fritzing sketch Breadboard (saved by Fritzing 0.9.3b)
circuit board: 8.46667cm x 5.64444cm
breadboards: 1

parts:
  IC1 = IC, DIP package, 14 pins [chip_label=MCP4922]
  IC2 = IC, DIP package, 14 pins [chip_label=TL074]
  R1 = Resistor [tolerance=±5% resistance=10k package=THT]
  R2 = Resistor [tolerance=±5% resistance=10k package=THT]
  R3 = Resistor [tolerance=±5% resistance=10k package=THT]
  R4 = Resistor [tolerance=±5% resistance=10k package=THT]
  R5 = Resistor [tolerance=±5% resistance=10k package=THT]
  R6 = Resistor [tolerance=±5% resistance=10k package=THT]
  R9 = Resistor [tolerance=±5% resistance=10k package=THT]
  R10 = Resistor [tolerance=±5% resistance=10k package=THT]
  IC4 = Voltage Regulator [package=to-92]
  R11 = Resistor [tolerance=±5% resistance=10k package=THT]
  R12 = Resistor [tolerance=±5% resistance=10k package=THT]
  R13 = Resistor [tolerance=±5% resistance=10k package=THT]
  R14 = Resistor [tolerance=±5% resistance=150 package=THT]
  R16 = Resistor [tolerance=±5% resistance=10k package=THT]
  R17 = Resistor [tolerance=±5% resistance=10k package=THT]
  R18 = Resistor [tolerance=±5% resistance=10k package=THT]
  R19 = Resistor [tolerance=±5% resistance=150 package=THT]
  C1 = Ceramic Capacitor [capacitance=22pF package="100 mil [THT, multilayer]"]
  C2 = Ceramic Capacitor [capacitance=22pF package="100 mil [THT, multilayer]"]
  IC5 = Voltage Regulator [package=to-92]

nets:
  N1: IC1.pin10, R4.Pin_0
  N2: IC1.pin14, R1.Pin_0
  N3: IC2.pin1, R6.Pin_1, R11.Pin_0
  N4: IC2.pin2, R4.Pin_1, R5.Pin_1
  N5: IC2.pin3, IC2.pin5, IC2.pin10, IC2.pin12, IC4.IN, IC5.IN
  N6: IC2.pin4, IC4.OUT, IC5.OUT
  N7: IC2.pin6, R9.Pin_0, R11.Pin_1, R12.Pin_0, C1.0
  N8: IC2.pin7, R13.Pin_1, R14.Pin_1, C1.1
  N9: IC2.pin8, R17.Pin_1, R19.Pin_1, C2.1
  N10: IC2.pin9, R10.Pin_0, R16.Pin_1, R18.Pin_0, C2.0
  N11: IC2.pin13, R1.Pin_1, R2.Pin_1
  N12: IC2.pin14, R3.Pin_1, R16.Pin_0
  N13: R2.Pin_0, R3.Pin_0
  N14: R5.Pin_0, R6.Pin_0
  N15: R9.Pin_1, IC4.GND
  N16: R10.Pin_1, IC5.GND
  N17: R12.Pin_1, R13.Pin_0
  N18: R17.Pin_0, R18.Pin_1
